// Logisim project 2 BIT Synchronous Counter.circ as structural Verilog: 1 circuit, main circuit main
module main (
  output out_1,
  output out_2
);

  wire clock_1_out, d_ff_1_qn, d_ff_2_qn, xor_1_out;

  Clock clock_1 (.out(clock_1_out));
  D_Flip_Flop d_ff_1 (.clk(clock_1_out), .D(d_ff_1_qn), .Q(out_2), .Qn(d_ff_1_qn));  // open: preset, en, reset
  xor xor_1 (xor_1_out, d_ff_2_qn, d_ff_1_qn);
  D_Flip_Flop d_ff_2 (.clk(clock_1_out), .D(xor_1_out), .Q(out_1), .Qn(d_ff_2_qn));  // open: preset, en, reset

  // Notes on the sheet:
  //   2 BIT Synchronous Counter
endmodule
