// Logisim project 4 Bit Multiplexer.circ as structural Verilog: 1 circuit, main circuit main
module main (
  input  A,
  input  B,
  input  C,
  input  D,
  input  b_2,
  input  a_2,
  output out_7
);

  wire nand_1_out, nand_2_out, nand_3_out, nand_4_out, nand_5_out, nand_6_out;

  nand nand_1 (nand_1_out, b_2, b_2);
  nand nand_2 (nand_2_out, a_2, a_2);
  nand nand_3 (nand_3_out, A, nand_1_out, nand_2_out);
  nand nand_4 (nand_4_out, B, nand_1_out, a_2);
  nand nand_5 (nand_5_out, C, nand_2_out, b_2);
  nand nand_6 (nand_6_out, D, b_2, a_2);
  nand nand_7 (out_7, nand_3_out, nand_4_out, nand_5_out, nand_6_out);

  // Notes on the sheet:
  //   b-
  //   a-
  //   Q
endmodule
