// Logisim project Asychronous Counter.circ as structural Verilog
module main (
  output out_1,
  output out_2,
  output out_3,
  output out_4,
  output out_5
);

  wire clock_1_out, clock_2_out, d_ff_1_qn, d_ff_2_qn, d_ff_3_qn, d_ff_4_qn, d_ff_5_qn, not_1_out, not_2_out;

  not not_1 (not_1_out, clock_1_out);
  Clock clock_1 (.out(clock_1_out));
  D_Flip_Flop d_ff_1 (.clk(not_1_out), .D(d_ff_1_qn), .Q(out_5), .Qn(d_ff_1_qn));  // open: preset, en, reset
  D_Flip_Flop d_ff_2 (.clk(d_ff_1_qn), .D(d_ff_2_qn), .Q(out_4), .Qn(d_ff_2_qn));  // open: preset, en, reset
  Clock clock_2 (.out(clock_2_out));
  D_Flip_Flop d_ff_3 (.clk(d_ff_2_qn), .D(d_ff_3_qn), .Q(out_3), .Qn(d_ff_3_qn));  // open: preset, en, reset
  not not_2 (not_2_out, clock_2_out);
  D_Flip_Flop d_ff_4 (.clk(not_2_out), .D(d_ff_4_qn), .Q(out_2), .Qn(d_ff_4_qn));  // open: preset, en, reset
  D_Flip_Flop d_ff_5 (.clk(d_ff_4_qn), .D(d_ff_5_qn), .Q(out_1), .Qn(d_ff_5_qn));  // open: preset, en, reset

  // Notes on the sheet:
  //   3 BIT Asynchronous Counter
  //   2 BIT Asynchronous Counter
endmodule
