// Logisim project Comparator.circ as structural Verilog: 1 circuit, main circuit main
module main (
  input  A,
  input  in_2,
  output a_2,
  output b,
  output c
);

  wire not_1_out, not_2_out;

  not not_1 (not_1_out, in_2);
  not not_2 (not_2_out, A);
  and and_1 (a_2, A, not_1_out);
  xnor xnor_1 (b, A, in_2);
  and and_2 (c, in_2, not_2_out);
endmodule
