// Logisim project Half Adder.circ as structural Verilog: 1 circuit, main circuit main
module main (
  input  in_1,
  input  in_2,
  output Sum,
  output Carry
);

  and and_1 (Sum, in_1, in_2);
  xor xor_1 (Carry, in_1, in_2);
endmodule
