// Logisim project Single Bit Multiplexer.circ as structural Verilog: 2 circuits, main circuit main
module main (
  input  Io,
  input  A,
  input  I1,
  output Q
);

  wire nand_1_out, nand_2_out, nand_3_out;

  nand nand_1 (nand_1_out, A, A);
  nand nand_2 (nand_2_out, Io, A);
  nand nand_3 (nand_3_out, nand_1_out, I1);
  nand nand_4 (Q, nand_2_out, nand_3_out);
endmodule

module top (
  input  in_1,
  input  in_2,
  input  in_3,
  input  in_4,
  input  [1:0] in_5,
  output out_6
);

  wire main_1_q, main_2_q;

  main main_1 (.Q(main_1_q), .Io(in_1), .I1(in_2), .A(in_5[0]));
  main main_2 (.Q(main_2_q), .Io(in_3), .I1(in_4), .A(in_5[0]));
  main main_3 (.Q(out_6), .Io(main_1_q), .I1(main_2_q), .A(in_5[1]));
endmodule
